# Fritzing sketch Arduino_moteur (saved by Fritzing 0.9.3b)
breadboards: 1

parts:
  Part1 = Arduino Uno (Rev3) - ICSP
  IC1 = L293D [package=THT]
  VCC1 = Battery block 9V
  VCC2 = Battery block 9V
  M1 = DC Motor
  C1 = Capacitor [package=cap-pth-small2]

nets:
  N1: Part1.D8, IC1.In_2
  N2: Part1.D7, IC1.In_1
  N3: Part1.5V, IC1.Enable_1
  N4: Part1.GND, IC1.0V, VCC2.-
  N5: IC1.Out_1_(_Controlled_by_Enable_1_), M1.pin_2, C1.1
  N6: IC1.Out_2_(_Controlled_by_Enable_1_), M1.pin_1, C1.2
  N7: IC1.+Vmotor, VCC1.+
  N8: VCC1.-, VCC2.+
