# Fritzing sketch Montage moteur l293d final (saved by Fritzing 0.9.3b)
breadboards: 2

parts:
  IC1 = L293D [package=THT]
  Composant1 = Arduino Uno (Rev3)
  M1 = DC Motor
  VCC1 = Battery block 9V

nets:
  N1: IC1.Enable_1, Composant1.5V
  N2: IC1.In_1, Composant1.D9_PWM
  N3: IC1.Out_1_(_Controlled_by_Enable_1_), M1.pin_1
  N4: IC1.0V, Composant1.GND, VCC1.-
  N5: IC1.In_2, Composant1.D8
  N6: IC1.+Vmotor, VCC1.+
