# Fritzing sketch Raspi_lcd (saved by Fritzing 0.9.3b)
breadboards: 1

parts:
  Raspberry_Pi_1 = Raspberry Pi 3 [part_number=RPI-3-V1.2]
  U1 = POT [package=pot_mammoth]
  LCD1 = LCD screen
  R1 = Resistor [tolerance=±5% resistance=220 package="0805 [SMD]"]

nets:
  N1: Raspberry_Pi_1.GPIO2, LCD1.RS
  N2: Raspberry_Pi_1.GPIO3, LCD1.E
  N3: Raspberry_Pi_1.GPIO4, LCD1.DB4
  N4: Raspberry_Pi_1.GPIO5, LCD1.DB5
  N5: Raspberry_Pi_1.GPIO6, LCD1.DB6
  N6: Raspberry_Pi_1.GPIO7, LCD1.DB7
  GND: Raspberry_Pi_1.GND, U1.S, LCD1.VSS, LCD1.R/W, LCD1.LED-
  5V: Raspberry_Pi_1.5V, U1.E, LCD1.VDD, R1.Pin_0
  N7: U1.A, LCD1.V0
  N8: LCD1.LED+, R1.Pin_1
